# Fritzing sketch board v1 (saved by Fritzing 0.9.10b)
perfboards: 2

parts:
  Debug_Button = Pushbutton [package="[SMD]"]
  I2S_-_Lock_Sensor = JST XH 4A 2.54mm [package=THT]
  I2S_-_Monitor = JST XH 4A 2.54mm [package=THT]
  WeMos_D1_Mini1 = WeMos D1 Mini
  PhotoSensor = male pin header, 2 pins [form="♂ (male)"]  # not connected
  J2 = male pin header, 3 pins [form="♂ (male)"]
  R1 = Resistor [tolerance=±5% power=0.25 resistance=10k package=THT]
  Indoor_Buzzer = Passive Buzzer
  Outdoor_Buzzer = Passive Buzzer
  Stop = smd LED [color="Red (633nm)" package="1206 [SMD]"]
  Go = LED - 5mm [color="Green (565nm)" current=0.030 package="5 mm [THT]"]
  Go_2 = LED - 5mm [color="Green (565nm)" current=0.030 package="5 mm [THT]"]
  Stop_2 = smd LED [color="Red (633nm)" package="1206 [SMD]"]
  R2 = Resistor [tolerance=±5% power=0.25 resistance=330 package=THT]
  R3 = Resistor [tolerance=±5% power=0.25 resistance=330 package=THT]
  R4 = Resistor [tolerance=±5% power=0.25 resistance=330 package=THT]
  R5 = Resistor [tolerance=±5% power=0.25 resistance=330 package=THT]
  In-Out_Door = JST XH 5A
  In-Out_Door_2 = JST XH 5A
  J3 = male pin header, 3 pins [form="♂ (male)"]
  R6 = Photocell (LDR) [package=THT]

nets:
  N1: Debug_Button.Pin_1, Debug_Button.Pin_2, I2S_-_Lock_Sensor.pin2, I2S_-_Monitor.pin2, WeMos_D1_Mini1.3V3, J2.pin3, Indoor_Buzzer.NC, R6.pin_0
  N2: Debug_Button.Pin_3, Debug_Button.Pin_4, WeMos_D1_Mini1.D8
  N3: I2S_-_Lock_Sensor.pin1, I2S_-_Monitor.pin1, WeMos_D1_Mini1.G
  N4: I2S_-_Lock_Sensor.pin3, I2S_-_Monitor.pin3, WeMos_D1_Mini1.D1
  N5: I2S_-_Lock_Sensor.pin4, I2S_-_Monitor.pin4, WeMos_D1_Mini1.D2
  N6: WeMos_D1_Mini1.A0, R1.Pin_0, R6.pin_1
  N7: WeMos_D1_Mini1.D0, J2.pin1, Indoor_Buzzer.S
  N8: J2.pin2, Indoor_Buzzer.-, In-Out_Door.pin2
  N9: Outdoor_Buzzer.S, In-Out_Door_2.pin3, J3.pin2
  N10: Outdoor_Buzzer.NC, In-Out_Door_2.pin1, J3.pin1
  N11: Outdoor_Buzzer.-, In-Out_Door_2.pin2, J3.pin3
  N12: Stop.cathode, Go.cathode, Go_2.cathode, Stop_2.cathode
  N13: Stop.anode, R5.Pin_1
  N14: Go.anode, R2.Pin_0
  N15: Go_2.anode, R3.Pin_1
  N16: Stop_2.anode, R4.Pin_0
  N17: R2.Pin_1, R3.Pin_0, In-Out_Door_2.pin4
  N18: R4.Pin_1, R5.Pin_0, In-Out_Door_2.pin5

notes:
  door_lock v1.1

custom parts:
  JST XH 4A 2.54mm: 4 Pin JST XH connector
  JST XH 5A: JST XH 5A 2.54.mm
